// Logisim project MiniRISCV.circ as structural Verilog: 4 circuits, main circuit main
module main (
  input  in_1,
  input  in_2
);

  wire alu_1_p5, clock_1_out, control_1_useimm, registerfile_1_p6;
  wire [3:0] control_1_aluop;
  wire [4:0] control_1_rd, control_1_rs1, control_1_rs2, sa_1_out_2;
  wire [7:0] registerfile_1_p1;
  wire [31:0] control_1_imm, multiplexer_1_out, pc_1_out_4, registerfile_1_p7, risc_vprogramrom_1_p2;

  PC pc_1 (.we(in_1), .clk(clock_1_out), .clr(in_2), .out_4(pc_1_out_4));
  Clock clock_1 (.out(clock_1_out));
  // RISC_VProgramROM risc_vprogramrom_1: pin names not known; wires that end beside it: pc_1_out_4, risc_vprogramrom_1_p2
  Control control_1 (
    .inst(risc_vprogramrom_1_p2), .rs1(control_1_rs1), .rs2(control_1_rs2), .rd(control_1_rd),
    .imm(control_1_imm), .useImm(control_1_useimm), .ALUop(control_1_aluop));
  // RegisterFile registerfile_1: pin names not known; wires that end beside it: registerfile_1_p1, clock_1_out, control_1_rd, control_1_rs1, control_1_rs2, registerfile_1_p6, registerfile_1_p7
  Multiplexer #(.width(32), .enable("false")) multiplexer_1 (
    .in0(registerfile_1_p7), .in1(control_1_imm), .out(multiplexer_1_out), .sel(control_1_useimm));
  SA sa_1 (.SA_32(multiplexer_1_out), .out_2(sa_1_out_2));
  // ALU alu_1: pin names not known; wires that end beside it: registerfile_1_p6, multiplexer_1_out, control_1_aluop, sa_1_out_2, alu_1_p5, alu_1_p5
  RAM ram_1 (.data(registerfile_1_p1), .clk(clock_1_out));  // open: addr, sel, ld, clr
endmodule

module PC (
  input  we,
  input  clk,
  input  clr,
  output [31:0] out_4
);

  wire [3:3] incrementer_1_p2;

  Register #(.width(32)) clk_in (
    .D({out_4[31:4], incrementer_1_p2[3], out_4[2:0]}), .en(we), .clk(clk), .Q(out_4), .clr(clr));
  // Incrementer #(.width(1)) incrementer_1: pin names not known; wires that end beside it: out_4[3], incrementer_1_p2[3]
endmodule

module Control (
  input  [31:0] inst,
  output [4:0] rs1,
  output [4:0] rs2,
  output [4:0] rd,
  output [31:0] imm,
  output useImm,
  output [3:0] ALUop
);

  // Decode_Black_Box decode_black_box_1: pin names not known; wires that end beside it: inst, rs1, rs2, rd, imm, useImm, ALUop
endmodule

module SA (
  input  [31:0] SA_32,
  output [4:0] out_2
);


  assign out_2 = SA_32[4:0];
endmodule
